# Fritzing sketch 05_Circuit_Diagram_ExpansionShield_ArduinoNano (saved by Fritzing 0.9.9b)

parts:
  LCM1602_IIC2 = LCM1602 IIC [part_number="LCM1602 IIC" chip_label="LCM1602 IIC" package="DIP (Dual Inline) [THT]"]
  U2 = LCD-16X2 [package=lcd-16x2_noholes]
  Componente1 = Arduino Nano (Rev3.0) (ICSP)
  VCC2 = Battery block 9V  # not connected
  DHT1 = DHT11 Humitidy and Temperature Sensor (3 pins)
  Mod1 = Nano-V3-0-IO-Expansion-Adapter
  J2 = Piezo Speaker
  Componente5 = Soil Moisture Sensor
  e-radionica_com1 = LM393 LDR breakout [part_number=100027]
  Mod2 = KY-011 Two Color LED Module [package="Breakout board"]

nets:
  VSS: LCM1602_IIC2.VSS, U2.VSS
  VDD: LCM1602_IIC2.VDD, U2.VDD
  N1: LCM1602_IIC2.V0, U2.VO
  N2: LCM1602_IIC2.RS, U2.RS
  N3: LCM1602_IIC2.RW, U2.R_W
  N4: LCM1602_IIC2.E, U2.E
  N5: LCM1602_IIC2.D0, U2.DB0
  N6: LCM1602_IIC2.D1, U2.DB1
  N7: LCM1602_IIC2.D2, U2.DB2
  N8: LCM1602_IIC2.D3, U2.DB3
  N9: LCM1602_IIC2.D4, U2.DB4
  N10: LCM1602_IIC2.D5, U2.DB5
  N11: LCM1602_IIC2.D6, U2.DB6
  N12: LCM1602_IIC2.D7, U2.DB7
  N13: LCM1602_IIC2.A, U2.A
  N14: LCM1602_IIC2.K, U2.K
  GND: LCM1602_IIC2.GND, Componente1.GND, DHT1.Gnd, Mod1.GND, J2.pin1, Componente5.GND, e-radionica_com1.GND, Mod2.-
  VCC: LCM1602_IIC2.VCC, Componente1.5V, DHT1.Plus, Mod1.VCC, Componente5.VCC, e-radionica_com1.VCC
  N15: LCM1602_IIC2.SDA, Componente1.A4, Mod1.A4/SDA
  N16: LCM1602_IIC2.SCL, Componente1.A5, Mod1.A5/SCL
  N17: LCM1602_IIC2.LED_A, LCM1602_IIC2.LED_B
  N18: Componente1.D1/TX, Mod1.D1/TX#65, Mod1.D0/RX#128
  N19: Componente1.D0/RX, Mod1.D0/RX#64, Mod1.D1/TX#129
  N20: Componente1.RESET, Mod1.RST
  N21: Componente1.D2, DHT1.Signal, Mod1.D2
  N22: Componente1.D3, Mod1.D3_PWM
  N23: Componente1.D4, Mod1.D4, Componente5.SIG
  N24: Componente1.D5, Mod1.D5_PWM
  N25: Componente1.D6, Mod1.D6_PWM
  N26: Componente1.D7, Mod1.D7
  N27: Componente1.D8, Mod1.D8, J2.pin2
  N28: Componente1.D9, Mod1.D9_PWM
  N29: Componente1.D10, Mod1.D10_PWM/SS, Mod2.S
  N30: Componente1.D11/MOSI, Mod1.D11_PWM/MOSI
  N31: Componente1.D12/MISO, Mod1.D12/MISO
  VIN: Componente1.VIN, Mod1.VIN
  N32: Componente1.A7, Mod1.A7
  N33: Componente1.A6, Mod1.A6
  N34: Componente1.A3, Mod1.A3
  N35: Componente1.A2, Mod1.A2
  N36: Componente1.A1, Mod1.A1, e-radionica_com1.AO
  N37: Componente1.A0, Mod1.A0
  N38: Componente1.AREF, Mod1.AREF
  N39: Componente1.3V3, Mod1.NC
  N40: Componente1.D13/SCK, Mod1.D13/SCK

custom parts:
  LCM1602 IIC: I2C-Module to use a 1602 or 2004 LCD on with the wire.h libory Serial LCD Modul
  DHT11 Humitidy and Temperature Sensor (3 pins): DHT11 Humidity and Temperature Sensor (3 pins).
  Nano-V3-0-IO-Expansion-Adapter: Nano V3.0 IO Expansion Adapter Shield. Note pcb view has been supressed as not useful. You can drag a Nano over the Nano connectors and it will connect and appear in schematic (although at present due to a bug, routing will not show as complete in breadboard).
  KY-011 Two Color LED Module: KY-011 Two Color LED Module consist of a common cathode 3mm red/green LED.
